// Logisim project 3BitShitft_JunHyungPark.circ as structural Verilog: 1 circuit, main circuit main
// Q2
module main (
  output Q2,
  output Q1,
  output Q0
);

  wire clock_1_out;

  Clock clock_1 (.out(clock_1_out));
  D_Flip_Flop DQ2 (.clk(clock_1_out), .D(Q0), .Q(Q2));  // open: Qn, preset, en, reset
  D_Flip_Flop DQ1 (.clk(clock_1_out), .D(Q2), .Q(Q1));  // open: Qn, preset, en, reset
  D_Flip_Flop DQ0 (.clk(clock_1_out), .D(Q1), .Q(Q0));  // open: Qn, preset, en, reset
endmodule
