// Logisim project Question3_6_circuit.circ as structural Verilog: 1 circuit, main circuit main
module main (
  input  X,
  input  Y,
  input  Z,
  output S,
  output C
);

  wire xor_1_out, XY_out, XZ_out, YZ_out;

  xor xor_1 (xor_1_out, X, Y);
  xor xor_2 (S, xor_1_out, Z);
  and YZ (YZ_out, Y, Z);
  and XY (XY_out, Y, X);
  and XZ (XZ_out, X, Z);
  or or_1 (C, YZ_out, XY_out, XZ_out);

  // Notes on the sheet:
  //   X XOR Y
  //   X XOR Y XOR Z
  //   YZ+XY+XZ
endmodule
