// Logisim project Question4_1_circuit.circ as structural Verilog: 1 circuit, main circuit main
module main (
  input  X,
  input  Y,
  output Z,
  output A,
  output B
);

  wire clock_1_out, not_1_out, not_2_out, nxA_out, nxB_out, nxB_xy_out, nXY_out, nxy_yB_out, X_nY_out,
       xy_out, yB_2_out, yB_nxA_out, yB_out;

  not not_1 (not_1_out, Y);
  not not_2 (not_2_out, X);
  and X_nY (X_nY_out, X, not_1_out);
  and nXY (nXY_out, not_2_out, Y);
  and yB (yB_out, Y, B);
  and nxB (nxB_out, not_2_out, B);
  and xy (xy_out, X, Y);
  and yB_2 (yB_2_out, Y, B);
  and nxA (nxA_out, not_2_out, A);
  or Y_X_nY (Z, X_nY_out, Y);
  or nxy_yB (nxy_yB_out, nXY_out, yB_out);
  or nxB_xy (nxB_xy_out, nxB_out, xy_out);
  or yB_nxA (yB_nxA_out, yB_2_out, nxA_out);
  Clock clock_1 (.out(clock_1_out));
  D_Flip_Flop d_ff_1 (.clk(clock_1_out), .D(nxy_yB_out), .Q(A));  // open: Qn, preset, en, reset
  J_K_Flip_Flop j_k_ff_1 (.J(nxB_xy_out), .clk(clock_1_out), .K(yB_nxA_out), .Q(B));  // open: Qn, preset, en, reset
endmodule
