// Logisim project Question5_4_circuit.circ as structural Verilog: 1 circuit, main circuit main
module main (
  input  in_1
);

  wire B_qn, C_qn, clock_1_out, nB_nC_out;

  Clock clock_1 (.out(clock_1_out));
  J_K_Flip_Flop A (.J(nB_nC_out), .clk(clock_1_out), .K(nB_nC_out));  // open: Q, Qn, preset, en, reset
  and nB_nC (nB_nC_out, C_qn, B_qn);
  J_K_Flip_Flop B (.J(C_qn), .clk(clock_1_out), .K(C_qn), .Qn(B_qn));  // open: Q, preset, en, reset
  J_K_Flip_Flop C (.J(in_1), .clk(clock_1_out), .K(in_1), .Qn(C_qn));  // open: Q, preset, en, reset

  // Notes on the sheet:
  //   Turn this To 1!!!
endmodule
